// Digital circuit ALU_OP.dig as structural Verilog
module ALU_OP (
  input  R,
  input  L,
  input  S,
  input  B,
  input  I,
  input  JARL,
  input  JAL,
  output [2:0] ALU_op
);

  and and_1 (ALU_op[0], ~R, ~B, ~I, ~JARL, ~JAL);  // And
  and and_2 (ALU_op[1], ~R, ~L, ~S, ~I);  // And
  and and_3 (ALU_op[2], ~R, ~L, ~B);  // And

  // Other names for the same wires on the sheet: JALR = JARL
endmodule
