// Digital circuit IdentificadorOP.dig as structural Verilog
module IdentificadorOP (
  input  [6:0] opcode,
  output R,
  output L,
  output S,
  output B,
  output I,
  output JALR,
  output JAL,
  output HALT
);

  Comparator #(.Bits(7)) comparator_1 (.a(7'b0110011), .b(opcode), .eq(R));  // open: gt, lt
  Comparator #(.Bits(7)) comparator_2 (.a(7'b0000011), .b(opcode), .eq(L));  // open: gt, lt
  Comparator #(.Bits(7)) comparator_3 (.a(7'b0100011), .b(opcode), .eq(S));  // open: gt, lt
  Comparator #(.Bits(7)) comparator_4 (.a(7'b1100011), .b(opcode), .eq(B));  // open: gt, lt
  Comparator #(.Bits(7)) comparator_5 (.a(7'b0010011), .b(opcode), .eq(I));  // open: gt, lt
  Comparator #(.Bits(7)) comparator_6 (.a(7'b1100111), .b(opcode), .eq(JALR));  // open: gt, lt
  Comparator #(.Bits(7)) comparator_7 (.a(7'b1101111), .b(opcode), .eq(JAL));  // open: gt, lt
  Comparator #(.Bits(7)) comparator_8 (.a(7'b0000001), .b(opcode), .eq(HALT));  // open: gt, lt

  // Other names for the same wires on the sheet: op[6:0] = opcode

  // Notes on the sheet:
  //   Jump-And-Link-Register
  //   Tipo de instrução
  //   Jump-And-Link
  //   STOP
  //   R-Type
  //   L-Type
  //   S-Type
  //   B-Type
  //   I-Type
  //   O valor lógico se o OPCode é ou não sobre
  //   o determinado tipo de instrução
endmodule
