// Digital circuit Imediato.dig as structural Verilog
module Imediato (
  input  [31:0] instruction,
  input  [31:0] ProgramCounter,
  output [31:0] S,
  output [31:0] B,
  output [31:0] I,
  output [31:0] J
);

  wire [31:0] bitextender_2_out, bitextender_3_out;

  BitExtender #(.inputBits(12), .outputBits(32)) bitextender_1 (.in({instruction[31:25], instruction[11:7]}), .out(S));
  BitExtender #(.inputBits(13), .outputBits(32)) bitextender_2 (
    .in({instruction[31], instruction[7], instruction[30:25], instruction[11:8], 1'b0}),
    .out(bitextender_2_out));
  BitExtender #(.inputBits(21), .outputBits(32)) bitextender_3 (
    .in({instruction[31], instruction[19:12], instruction[20], instruction[30:21], 1'b0}),
    .out(bitextender_3_out));
  BitExtender #(.inputBits(12), .outputBits(32)) bitextender_4 (.in(instruction[31:20]), .out(I));
  Add #(.Bits(32)) add_1 (.a(bitextender_3_out), .b(ProgramCounter), .c_i(1'b0), .s(J));  // open: c_o
  Add #(.Bits(32)) add_2 (.a(bitextender_2_out), .b(ProgramCounter), .c_i(1'b0), .s(B));  // open: c_o

  // Other names for the same wires on the sheet: inst[31:0] = instruction; pc[31:0] = ProgramCounter
endmodule
