// Digital circuit RegisterBank.dig as structural Verilog
module RegisterBank (
  input  CLK,
  input  [4:0] A,
  input  [4:0] B,
  input  [4:0] Enable,
  input  [31:0] C,
  output [31:0] ReadData1,
  output [31:0] ReadData2
);

  wire demultiplexer_1_out_1, demultiplexer_1_out_2, demultiplexer_1_out_3, demultiplexer_1_out_4,
       demultiplexer_1_out_5, demultiplexer_1_out_6, demultiplexer_1_out_7, demultiplexer_1_out_8,
       demultiplexer_1_out_9, demultiplexer_1_out_10, demultiplexer_1_out_11, demultiplexer_1_out_12,
       demultiplexer_1_out_13, demultiplexer_1_out_14, demultiplexer_1_out_15, demultiplexer_1_out_16,
       demultiplexer_1_out_17, demultiplexer_1_out_18, demultiplexer_1_out_19, demultiplexer_1_out_20,
       demultiplexer_1_out_21, demultiplexer_1_out_22, demultiplexer_1_out_23, demultiplexer_1_out_24,
       demultiplexer_1_out_25, demultiplexer_1_out_26, demultiplexer_1_out_27, demultiplexer_1_out_28,
       demultiplexer_1_out_29, demultiplexer_1_out_30, demultiplexer_1_out_31;
  wire [31:0] b2, b3, b4, b5, b6, b7, b8, b9, b10, b11, b12, b13, b14, b15, b16, b17, b18, b19, b20, b21,
       b22, b23, b24, b25, b26, b27, b28, b29, b30, b31, b32;

  Demultiplexer #(.Selector_Bits(5)) demultiplexer_1 (
    .sel(Enable), .in(1'b1), .out_1(demultiplexer_1_out_1), .out_2(demultiplexer_1_out_2),
    .out_3(demultiplexer_1_out_3), .out_4(demultiplexer_1_out_4), .out_5(demultiplexer_1_out_5),
    .out_6(demultiplexer_1_out_6), .out_7(demultiplexer_1_out_7), .out_8(demultiplexer_1_out_8),
    .out_9(demultiplexer_1_out_9), .out_10(demultiplexer_1_out_10), .out_11(demultiplexer_1_out_11),
    .out_12(demultiplexer_1_out_12), .out_13(demultiplexer_1_out_13), .out_14(demultiplexer_1_out_14),
    .out_15(demultiplexer_1_out_15), .out_16(demultiplexer_1_out_16), .out_17(demultiplexer_1_out_17),
    .out_18(demultiplexer_1_out_18), .out_19(demultiplexer_1_out_19), .out_20(demultiplexer_1_out_20),
    .out_21(demultiplexer_1_out_21), .out_22(demultiplexer_1_out_22), .out_23(demultiplexer_1_out_23),
    .out_24(demultiplexer_1_out_24), .out_25(demultiplexer_1_out_25), .out_26(demultiplexer_1_out_26),
    .out_27(demultiplexer_1_out_27), .out_28(demultiplexer_1_out_28), .out_29(demultiplexer_1_out_29),
    .out_30(demultiplexer_1_out_30), .out_31(demultiplexer_1_out_31));  // open: out_0
  Register #(.Bits(32)) register_1 (.D(C), .C(CLK), .en(demultiplexer_1_out_1), .Q(b2));
  Register #(.Bits(32)) register_2 (.D(C), .C(CLK), .en(demultiplexer_1_out_2), .Q(b3));
  Register #(.Bits(32)) register_3 (.D(C), .C(CLK), .en(demultiplexer_1_out_3), .Q(b4));
  Register #(.Bits(32)) register_4 (.D(C), .C(CLK), .en(demultiplexer_1_out_4), .Q(b5));
  Register #(.Bits(32)) register_5 (.D(C), .C(CLK), .en(demultiplexer_1_out_5), .Q(b6));
  Register #(.Bits(32)) register_6 (.D(C), .C(CLK), .en(demultiplexer_1_out_6), .Q(b7));
  Register #(.Bits(32)) register_7 (.D(C), .C(CLK), .en(demultiplexer_1_out_7), .Q(b8));
  Register #(.Bits(32)) register_8 (.D(C), .C(CLK), .en(demultiplexer_1_out_8), .Q(b9));
  Register #(.Bits(32)) register_9 (.D(C), .C(CLK), .en(demultiplexer_1_out_9), .Q(b10));
  Register #(.Bits(32)) register_10 (.D(C), .C(CLK), .en(demultiplexer_1_out_10), .Q(b11));
  Register #(.Bits(32)) register_11 (.D(C), .C(CLK), .en(demultiplexer_1_out_11), .Q(b12));
  Register #(.Bits(32)) register_12 (.D(C), .C(CLK), .en(demultiplexer_1_out_12), .Q(b13));
  Register #(.Bits(32)) register_13 (.D(C), .C(CLK), .en(demultiplexer_1_out_13), .Q(b14));
  Register #(.Bits(32)) register_14 (.D(C), .C(CLK), .en(demultiplexer_1_out_14), .Q(b15));
  Register #(.Bits(32)) register_15 (.D(C), .C(CLK), .en(demultiplexer_1_out_15), .Q(b16));
  Register #(.Bits(32)) register_16 (.D(C), .C(CLK), .en(demultiplexer_1_out_16), .Q(b17));
  Register #(.Bits(32)) register_17 (.D(C), .C(CLK), .en(demultiplexer_1_out_17), .Q(b18));
  Register #(.Bits(32)) register_18 (.D(C), .C(CLK), .en(demultiplexer_1_out_18), .Q(b19));
  Register #(.Bits(32)) register_19 (.D(C), .C(CLK), .en(demultiplexer_1_out_19), .Q(b20));
  Register #(.Bits(32)) register_20 (.D(C), .C(CLK), .en(demultiplexer_1_out_20), .Q(b21));
  Register #(.Bits(32)) register_21 (.D(C), .C(CLK), .en(demultiplexer_1_out_21), .Q(b22));
  Register #(.Bits(32)) register_22 (.D(C), .C(CLK), .en(demultiplexer_1_out_22), .Q(b23));
  Register #(.Bits(32)) register_23 (.D(C), .C(CLK), .en(demultiplexer_1_out_23), .Q(b24));
  Register #(.Bits(32)) register_24 (.D(C), .C(CLK), .en(demultiplexer_1_out_24), .Q(b25));
  Register #(.Bits(32)) register_25 (.D(C), .C(CLK), .en(demultiplexer_1_out_25), .Q(b26));
  Register #(.Bits(32)) register_26 (.D(C), .C(CLK), .en(demultiplexer_1_out_26), .Q(b27));
  Register #(.Bits(32)) register_27 (.D(C), .C(CLK), .en(demultiplexer_1_out_27), .Q(b28));
  Register #(.Bits(32)) register_28 (.D(C), .C(CLK), .en(demultiplexer_1_out_28), .Q(b29));
  Register #(.Bits(32)) register_29 (.D(C), .C(CLK), .en(demultiplexer_1_out_29), .Q(b30));
  Register #(.Bits(32)) register_30 (.D(C), .C(CLK), .en(demultiplexer_1_out_30), .Q(b31));
  Register #(.Bits(32)) register_31 (.D(C), .C(CLK), .en(demultiplexer_1_out_31), .Q(b32));
  Multiplexer #(.Bits(32), .Selector_Bits(5)) multiplexer_1 (
    .sel(A), .in_0({32{1'b0}}), .in_1(b2), .in_2(b3), .in_3(b4), .in_4(b5), .in_5(b6), .in_6(b7), .in_7(b8),
    .in_8(b9), .in_9(b10), .in_10(b11), .in_11(b12), .in_12(b13), .in_13(b14), .in_14(b15), .in_15(b16),
    .in_16(b17), .in_17(b18), .in_18(b19), .in_19(b20), .in_20(b21), .in_21(b22), .in_22(b23), .in_23(b24),
    .in_24(b25), .in_25(b26), .in_26(b27), .in_27(b28), .in_28(b29), .in_29(b30), .in_30(b31), .in_31(b32),
    .out(ReadData1));
  Multiplexer #(.Selector_Bits(5), .Bits(32)) multiplexer_2 (
    .sel(B), .in_0({32{1'b0}}), .in_1(b2), .in_2(b3), .in_3(b4), .in_4(b5), .in_5(b6), .in_6(b7), .in_7(b8),
    .in_8(b9), .in_9(b10), .in_10(b11), .in_11(b12), .in_12(b13), .in_13(b14), .in_14(b15), .in_15(b16),
    .in_16(b17), .in_17(b18), .in_18(b19), .in_19(b20), .in_20(b21), .in_21(b22), .in_22(b23), .in_23(b24),
    .in_24(b25), .in_25(b26), .in_26(b27), .in_27(b28), .in_28(b29), .in_29(b30), .in_30(b31), .in_31(b32),
    .out(ReadData2));

  // Other names for the same wires on the sheet: rd1[31:0] = ReadData1; rd2[31:0] = ReadData2; rr1[4:0] = A;
  //   rr2[4:0] = B; wd[31:0] = C; wr[4:0] = Enable
endmodule
