// Digital circuit TrabalhoProjetos.dig as structural Verilog
module TrabalhoProjetos (
  input  [31:0] A,
  input  [31:0] B,
  input  [2:0] FUNC3,
  input  [6:0] FUNC7,
  output [31:0] OUT
);

  wire and_1_out, and_2_out, and_3_out, and_4_out, and_5_out, and_6_out, multiplexer_2_out, or_1_out;
  wire [31:0] add_1_s, and_8_out, barrelshifter_1_out, multiplexer_1_out, not_1_out, or_2_out, xor_1_out;
  wire [31:31] undriven;

  and and_1 (and_1_out, ~FUNC3[0], ~FUNC3[1], ~FUNC3[2]);  // And
  and and_2 (and_2_out, ~FUNC7[6], FUNC7[5], ~FUNC7[4], ~FUNC7[3], ~FUNC7[2], ~FUNC7[1], ~FUNC7[0]);  // And
  and and_3 (and_3_out, ~FUNC3[2], FUNC3[1], ~FUNC3[0]);  // And
  and and_4 (and_4_out, ~FUNC7[6], ~FUNC7[5], ~FUNC7[4], ~FUNC7[3], ~FUNC7[2], ~FUNC7[1], ~FUNC7[0]);  // And
  and and_5 (and_5_out, ~FUNC3[0], ~FUNC3[1], FUNC3[2]);  // And
  and and_6 (and_6_out, and_1_out, and_2_out);
  // And and_7 has open pins: In_1=and_4_out, In_2=and_5_out, out=open
  or or_1 (or_1_out, and_6_out, and_3_out);
  BarrelShifter #(.Bits(32)) barrelshifter_1 (.in(A), .shift(B), .out(barrelshifter_1_out));
  assign and_8_out = A & B;  // And and_8, 32 bits wide
  assign or_2_out = A | B;  // Or or_2, 32 bits wide
  assign xor_1_out = A ^ B;  // XOr xor_1, 32 bits wide
  Multiplexer #(.Bits(32)) multiplexer_1 (.sel(or_1_out), .in_0(B), .in_1(not_1_out), .out(multiplexer_1_out));
  assign not_1_out = ~B;  // Not not_1, 32 bits wide
  Multiplexer multiplexer_2 (.sel(or_1_out), .in_0(1'b0), .in_1(1'b1), .out(multiplexer_2_out));
  Add #(.Bits(32)) add_1 (.a(A), .b(multiplexer_1_out), .c_i(multiplexer_2_out), .s(add_1_s));  // open: c_o
  Multiplexer #(.Selector_Bits(3), .Bits(32)) multiplexer_3 (
    .sel(3'b001), .in_0(add_1_s), .in_1(add_1_s), .in_2(xor_1_out), .in_3(or_2_out), .in_4(and_8_out),
    .in_5({undriven[31], add_1_s[30:0]}), .in_6(barrelshifter_1_out), .in_7({32{1'b0}}), .out(OUT));
  // Pins of 31 and 32 bits meet at {undriven[31], add_1_s[30:0]}
endmodule
