// Digital circuit UnidadeDeControle.dig as structural Verilog
module UnidadeDeControle (
  input  [6:0] Opcode,
  output memoryWrite,
  output Branch,
  output memoryRead,
  output registerWrite,
  output load_en,
  output [2:0] ALU_OP,
  output [1:0] A,
  output B,
  output [1:0] NExt_PC,
  output [1:0] extender
);

  wire HALT, I, JAL, JALR;

  IdentificadorOP identificadorop_1 (
    .opcode(Opcode), .R(memoryWrite), .L(load_en), .S(extender[1]), .B(Branch), .I(I), .JALR(JALR),
    .JAL(JAL), .HALT(HALT));
  ALU_OP alu_op_1 (
    .R(memoryWrite), .L(load_en), .S(extender[1]), .B(Branch), .I(I), .JARL(JALR), .JAL(JAL), .ALU_op(ALU_OP));
  next_PC next_pc_1 (.B(JAL), .JAL(JAL), .JARL(JALR), .next_PC(NExt_PC));
  xor xor_1 (A[1], JALR, JAL);
  or or_1 (registerWrite, memoryWrite, load_en, I, JALR, JAL);
  or or_2 (B, memoryWrite, extender[1], I);

  assign A[0] = 1'b0;
  assign extender[0] = 1'b0;
  assign memoryRead = load_en;

  // Other names for the same wires on the sheet: ALU[2:0] = ALU_OP; B_t = Branch; L = load_en; NEXT[1:0] = NExt_PC;
  //   R = memoryWrite; S = extender[1]
endmodule
