// Digital circuit UnidadeDeControle2.dig as structural Verilog
module UnidadeDeControle2 (
  input  [6:0] Opcode
);

  wire B, HALT, I, JAL, JALR, L, R, S;

  IdentificadorOP identificadorop_1 (
    .opcode(Opcode), .R(R), .L(L), .S(S), .B(B), .I(I), .JALR(JALR), .JAL(JAL), .HALT(HALT));
endmodule
