// Digital circuit next_PC.dig as structural Verilog
module next_PC (
  input  B,
  input  JAL,
  input  JARL,
  output [1:0] next_PC
);

  wire and_1_out, and_2_out, and_3_out, and_4_out;

  and and_1 (and_1_out, ~B, ~JARL, JAL);  // And
  and and_2 (and_2_out, ~B, JAL, ~JARL);  // And
  and and_3 (and_3_out, ~B, ~JAL, JARL);  // And
  and and_4 (and_4_out, B, ~JAL, ~JARL);  // And
  or or_1 (next_PC[1], and_1_out, and_2_out);
  or or_2 (next_PC[0], and_3_out, and_4_out);
endmodule
